// Logisim project cpu.circ as structural Verilog: 4 circuits, main circuit CPU
module CPU (
);

  wire [15:0] rom_1_data;

  Instruction_Decoder instruction_decoder_1 (.Instruction(rom_1_data));  // open: Opcode, RS, RT, RD, Immediate
  ROM #(.dataWidth(16)) rom_1 (.data(rom_1_data));  // open: addr, sel
  RAM ram_1 ();  // open: addr, data, sel, clk, ld, clr
endmodule

module Instruction_Decoder (
  input  [15:0] Instruction,
  output [3:0] Opcode,
  output [1:0] RS,
  output [1:0] RT,
  output [1:0] RD,
  output [7:0] Immediate
);


  assign Immediate = Instruction[7:0];
  assign Opcode = Instruction[15:12];
  assign RD = Instruction[7:6];
  assign RS = Instruction[11:10];
  assign RT = Instruction[9:8];
endmodule

module Register_File (
  input  [7:0] Write_Data,
  input  Clock,
  input  Write_Enable,
  input  [1:0] Read_Register_1,
  input  [1:0] Write_Address,
  input  [1:0] Read_Register_2,
  output [7:0] Read_Data_1,
  output [7:0] Read_Data_2
);

  wire and_1_out, and_2_out, and_3_out, and_4_out, decoder_1_out0, decoder_1_out1, decoder_1_out2,
       decoder_1_out3;
  wire [7:0] R0_q, R1_q, R2_q, R3_q;

  Decoder #(.select(2)) decoder_1 (
    .out0(decoder_1_out0), .out1(decoder_1_out1), .out2(decoder_1_out2), .out3(decoder_1_out3),
    .sel(Write_Address));  // open: en
  and and_1 (and_1_out, Write_Enable, decoder_1_out0);
  and and_2 (and_2_out, Write_Enable, decoder_1_out1);
  and and_3 (and_3_out, Write_Enable, decoder_1_out2);
  and and_4 (and_4_out, Write_Enable, decoder_1_out3);
  Register R0 (.D(Write_Data), .en(and_1_out), .Q(R0_q), .clk(Clock));  // open: clr
  Register R1 (.D(Write_Data), .en(and_2_out), .Q(R1_q), .clk(Clock));  // open: clr
  Register R2 (.D(Write_Data), .en(and_3_out), .Q(R2_q), .clk(Clock));  // open: clr
  Register R3 (.D(Write_Data), .en(and_4_out), .Q(R3_q), .clk(Clock));  // open: clr
  Multiplexer #(.select(2), .width(8)) multiplexer_1 (
    .in0(R0_q), .in1(R1_q), .in2(R2_q), .in3(R3_q), .out(Read_Data_1), .sel(Read_Register_1));  // open: en
  Multiplexer #(.select(2), .width(8)) multiplexer_2 (
    .in0(R0_q), .in1(R1_q), .in2(R2_q), .in3(R3_q), .out(Read_Data_2), .sel(Read_Register_2));  // open: en
endmodule

module ALU (
  input  [7:0] Data_A,
  input  [1:0] Select,
  input  [7:0] Data_B,
  output [7:0] Output,
  output Branch,
  output Zero_Dectector
);

  wire comparator_1_gt, comparator_1_lt, not_1_out;
  wire [7:0] adder_1_out, and_1_out, nor_1_out, subtractor_1_out;

  assign and_1_out = Data_A & Data_B;  // AND_Gate and_1, 8 bits wide
  assign nor_1_out = ~(Data_A | Data_B);  // NOR_Gate nor_1, 8 bits wide
  Adder adder_1 (.a(Data_A), .b(Data_B), .out(adder_1_out));  // open: cin, cout
  Subtractor subtractor_1 (.a(Data_A), .b(Data_B), .out(subtractor_1_out));  // open: bin, bout
  Comparator comparator_1 (.a(Data_A), .b({8{1'b0}}), .gt(comparator_1_gt), .eq(Zero_Dectector), .lt(comparator_1_lt));
  Multiplexer #(.select(2), .width(8), .enable("false")) multiplexer_1 (
    .in0(and_1_out), .in1(nor_1_out), .in2(adder_1_out), .in3(subtractor_1_out), .out(Output), .sel(Select));
  not not_1 (not_1_out, Zero_Dectector);
  Multiplexer #(.select(2), .enable("false")) multiplexer_2 (
    .in0(comparator_1_gt), .in1(Zero_Dectector), .in2(comparator_1_lt), .in3(not_1_out), .out(Branch),
    .sel(Select));
endmodule
